# Fritzing sketch DFPLAYER_Generica_standalone (saved by Fritzing 0.9.2b)
circuit board: 5.23543cm x 4.44697cm
breadboards: 1

parts:
  C1 = Electrolytic Capacitor [capacitance=1µF package="100 mil [THT, electrolytic]"]
  C2 = Ceramic Capacitor [capacitance=100nF package="100 mil [THT, multilayer]"]
  J1 = female pin header, 2 pins [form="♀ (female)"]
  J2 = female pin header, 2 pins [form="♀ (female)"]
  J3 = female pin header, 2 pins [form="♀ (female)"]
  R1 = Resistor [tolerance=±5% resistance=220 package=THT]
  R2 = Resistor [tolerance=±5% resistance=220 package=THT]
  R3 = Resistor [tolerance=±5% resistance=220 package=THT]
  R4 = Resistor [tolerance=±5% resistance=220 package=THT]
  R5 = Resistor [tolerance=±5% resistance=220 package=THT]
  R6 = Resistor [tolerance=±5% resistance=220 package=THT]
  R7 = Resistor [tolerance=±5% resistance=220 package=THT]
  R8 = Resistor [tolerance=±5% resistance=220 package=THT]
  R9 = Resistor [tolerance=±5% resistance=220 package=THT]
  R10 = Resistor [tolerance=±5% resistance=220 package=THT]
  R11 = Resistor [tolerance=±5% resistance=220 package=THT]
  R12 = Resistor [tolerance=±5% resistance=220 package=THT]
  R13 = Resistor [tolerance=±5% resistance=220 package=THT]
  R14 = Resistor [tolerance=±5% resistance=220 package=THT]
  R15 = Resistor [tolerance=±5% resistance=220 package=THT]
  R16 = Resistor [tolerance=±5% resistance=220 package=THT]
  R17 = Resistor [tolerance=±5% resistance=220 package=THT]
  R18 = Resistor [tolerance=±5% resistance=220 package=THT]
  R19 = Resistor [tolerance=±5% resistance=220 package=THT]
  R20 = Resistor [tolerance=±5% resistance=220 package=THT]
  J4 = double row female pin header, 38 pins [form="♀ (female)"]
  J5 = female pin header, 2 pins [form="♀ (female)"]
  DFRobot_DFPlayer_Mini1 = DFRobot DFPlayer Mini [part_number=DFR0299]

nets:
  N1: C1.+, C2.0, J1.pin1, J2.pin2, DFRobot_DFPlayer_Mini1.VCC
  N2: J1.pin2, J2.pin1, J4.pin20, J4.pin21, J4.pin22, J4.pin23, J4.pin24, J4.pin25, J4.pin26, J4.pin27, J4.pin28, J4.pin29, J4.pin30, J4.pin31, J4.pin32, J4.pin33, J4.pin34, J4.pin35, J4.pin36, J4.pin37, J4.pin38, DFRobot_DFPlayer_Mini1.GND-1, DFRobot_DFPlayer_Mini1.GND-2
  N3: J3.pin1, DFRobot_DFPlayer_Mini1.SPK_1
  N4: J3.pin2, DFRobot_DFPlayer_Mini1.SPK_2
  N5: R1.Pin_1, J4.pin19
  N6: R2.Pin_1, J4.pin18
  N7: R3.Pin_0, R4.Pin_0, R6.Pin_0, R9.Pin_0, R11.Pin_0, R12.Pin_0, DFRobot_DFPlayer_Mini1.ADKEY_1
  N8: R3.Pin_1, J4.pin17
  N9: R4.Pin_1, J4.pin16
  N10: R5.Pin_1, J4.pin15
  N11: R6.Pin_1, J4.pin14
  N12: R7.Pin_0, R8.Pin_0, R14.Pin_0, R15.Pin_0, R16.Pin_0, R17.Pin_0, R18.Pin_0, R19.Pin_0
  N13: R7.Pin_1, J4.pin9
  N14: R8.Pin_1, J4.pin8
  N15: R9.Pin_1, J4.pin10
  N16: R10.Pin_1, J4.pin12
  N17: R11.Pin_1, J4.pin13
  N18: R12.Pin_1, J4.pin11
  N19: R13.Pin_1, J4.pin7
  N20: R14.Pin_1, J4.pin6
  N21: R15.Pin_1, J4.pin5
  N22: R16.Pin_1, J4.pin4
  N23: R17.Pin_1, J4.pin3
  N24: R18.Pin_1, J4.pin2
  N25: R19.Pin_1, J4.pin1
  N26: R20.Pin_0, J5.pin1
  N27: R20.Pin_1, DFRobot_DFPlayer_Mini1.ADKEY_2
